# Fritzing sketch watchdog_fritzing (saved by Fritzing 0.9.3b)
breadboards: 1

parts:
  Part1 = Arduino Uno (Rev3)
  LCD1 = LCD screen
  Buzzer = Piezo Speaker
  MQ4_Sensor = GAS_SENSOR [package=mq-3]
  Q1 = NPN-Transistor [package="TO92 [THT]"]
  HC-O5_Bluetooth_Module = Bluetooth HC-05 Macho
  R1 = Resistor [tolerance=±5% resistance=1k package=THT]
  R2 = Resistor [tolerance=±5% resistance=410 package=THT]
  R4 = Resistor [tolerance=±5% resistance=410 package=THT]
  R5 = Resistor [tolerance=±5% resistance=410 package=THT]
  R3 = Resistor [tolerance=±5% resistance=410 package=THT]
  LED1 = LED - 5mm [color="Red (633nm)" package="5 mm [THT]"]

nets:
  N1: Part1.D8, R1.Pin_0, R2.Pin_0
  N2: Part1.D9_PWM, HC-O5_Bluetooth_Module.TXD
  N3: Part1.D10_PWM/SS, R5.Pin_0
  N4: Part1.D11_PWM/MOSI, LCD1.E
  N5: Part1.D12/MISO, LCD1.RS
  N6: Part1.D13/SCK, LED1.anode
  N7: Part1.D2, LCD1.DB7
  N8: Part1.D3_PWM, LCD1.DB6
  N9: Part1.D4, LCD1.DB5
  N10: Part1.D5_PWM, LCD1.DB4
  N11: Part1.D7, MQ4_Sensor.H2
  5V: Part1.5V, LCD1.VDD, Buzzer.pin2, MQ4_Sensor.A1, HC-O5_Bluetooth_Module.VCC
  GND: Part1.GND, LCD1.VSS, MQ4_Sensor.B1, Q1.E, HC-O5_Bluetooth_Module.GND, R4.Pin_1, R3.Pin_1, LED1.cathode
  N12: Buzzer.pin1, Q1.C
  N13: Q1.B, R1.Pin_1, R2.Pin_1
  N14: HC-O5_Bluetooth_Module.RXD, R4.Pin_0, R5.Pin_1, R3.Pin_0

// code stored in the sketch: last.ino
#include <SoftwareSerial.h>
#include <LiquidCrystal.h>
LiquidCrystal lcd(12, 11, 5, 4, 3, 2); 
SoftwareSerial mySerial(9,10);//Rx TX

int sensor=7;
int speaker=8;
int gas_value,Gas_alert_val, Gas_shut_val;
int Gas_Leak_Status;
int bl_data=0;
int bt_confirm=1;
int scandelay=500;
int led=13;
void setup()
{


pinMode(sensor,INPUT);
pinMode(speaker,OUTPUT);
pinMode(led,OUTPUT);


lcd.begin(16,2);
lcd.clear();
mySerial.begin(9600);   
mySerial.println("Bluetooth Connected..");


digitalWrite(speaker,HIGH);
delay(250); 
digitalWrite(speaker,LOW); 
delay(100);            //microcontroller reset buzz
digitalWrite(speaker,HIGH);
delay(250); 
digitalWrite(speaker,LOW); 
}

void loop()
{
CheckGas();

}

void CheckGas()
{

lcd.clear();
scannning_lcd_ani();
Gas_alert_val=ScanGasLevel();
if(Gas_alert_val==LOW)
{
 SetAlert(); 
}
}

int ScanGasLevel()
{
gas_value=digitalRead(sensor); // reads the sensor output

return gas_value; 
}

void SetAlert()

{
  
  set_alert_display_and_beep();
  
  if(CheckShutDown()!=0){
    lcd.clear();
    lcd.setCursor(3,0);
    lcd.print("BLUETOOTH");
    lcd.setCursor(4,1);
    lcd.print("ALERTING");
    led_alert();
	delay(1000);

    if(bl_data==0){
    serial_bluetooth();
    }
	else{
	lcd.clear();
	lcd.print("BLUETOOTH");
    lcd.setCursor(0,1);
    lcd.print("ALERTED");
    led_alert();
	delay(1000);
	}
    
    
    CheckShutDown();
  }
  
  
}

int CheckShutDown()
{
Gas_shut_val=ScanGasLevel();
if(Gas_shut_val==HIGH)
{
lcd.clear();
lcd.setCursor(0,0);
lcd.print("NO GAS LEAKING");
lcd.setCursor(6,1);
lcd.print("Now");
delay(5000);
return 0;
}
else 
  return 1;
}

void scannning_lcd_ani(){
  
    lcd.setCursor(0,0);
    lcd.print("    SCANNING");
    delay(scandelay);
    lcd.setCursor(7,1);
    lcd.print("()");
    delay(scandelay);
    lcd.setCursor(6,1);
    lcd.print("(())");
    delay(scandelay);
    lcd.setCursor(5,1);
    lcd.print("((()))");
    delay(scandelay);
    lcd.setCursor(4,1);
    lcd.print("(((())))");
    delay(scandelay);
    
}
void set_alert_display_and_beep(){
  lcd.clear();
  lcd.setCursor(1,0);
  lcd.print("!!GAS LEAKED!!");
  int count=20;
  while(count>0){
    led_alert();
    digitalWrite(speaker,HIGH);
    delay(150);
    digitalWrite(speaker,LOW);
    count--;
    delay(1000);
  }
  
 
  
}

void serial_bluetooth(){

    led_alert();
    mySerial.println("!!GAS LEAKED ON KITCHEN!!");
    if(mySerial.available()){
		bl_data = mySerial.read();
	}
    delay(100);
    
    
   }
  
    
void led_alert(){

  digitalWrite(13, HIGH);  
  delay(25);             
  digitalWrite(13, LOW); 
  digitalWrite(13, HIGH);  
  delay(25);             
  digitalWrite(13, LOW);   
  
}
